# Fritzing sketch L06_Encoder (saved by Fritzing 0.9.4)
breadboards: 1

parts:
  Part1 = 12 NeoPixel Ring [part_number=1643]
  Part2 = ws2812b [package="smd 2812b"]
  Teensy_3_1 = Teensy 3.1
  Part3 = ws2812b [package="smd 2812b"]
  Part4 = ws2812b [package="smd 2812b"]
  Part5 = ws2812b [package="smd 2812b"]
  U1 = ENCODER_2LED [package=encoder_led_2]

nets:
  N1: Part1.IN, Teensy_3_1.A3/D17
  N2: Part1.OUT, Part5.DIN
  VDD: Part1.VDD, Part2.VDD, Teensy_3_1.Vin, Part3.VDD, Part4.VDD, Part5.VDD
  VSS: Part1.GND, Part2.VSS, Teensy_3_1.GND, Part3.VSS, Part4.VSS, Part5.VSS, U1.C, U1.-
  N3: Part2.DIN, Part3.DOUT
  N4: Teensy_3_1.D0, U1.B
  N5: Teensy_3_1.D1, U1.A
  N6: Teensy_3_1.A6/D20, U1.SW
  N7: Teensy_3_1.A7/D21, U1.+G
  N8: Teensy_3_1.A8/D22, U1.+R
  N9: Part3.DIN, Part4.DOUT
  N10: Part4.DIN, Part5.DOUT

notes:
  Warning: This is not the encoder we are using in class. Follow instructions in the code files for wiring

custom parts:
  12 NeoPixel Ring: 12 ultra bright smart LED NeoPixels are arranged in a circle with 1.5" (37mm) outer diameter. The rings are 'chainable' - connect the output pin of one to the input pin of another. Use only one microcontroller pin to control as many as you can chain together! Each LED is addressable as the driver chip is inside the LED. Each one has ~18mA constant current drive so the color will be very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
